# Fritzing sketch sattrack (saved by Fritzing 0.9.2b)
breadboards: 1

parts:
  Part1 = Adafruit Feather M0 Basic Proto [part_number="Adafruit #2772"]
  Part3 = Adafruit DS3231 [part_number="Adafruit #3013"]
  Part4 = I2C Non-Volatile FRAM 32KB
  Grove1 = Grove OLED 128x96

nets:
  GND: Part1.GND, Part3.GND, Part4.GND, Grove1.GND
  VCC: Part1.+3V3, Part3.Vin, Part4.VCC, Grove1.VCC
  N1: Part1.SCL, Part3.SCL, Part4.SCL, Grove1.SCL
  N2: Part1.SDA, Part3.SDA, Part4.SDA, Grove1.SDA

notes:
  I2C
  VCC/GND

custom parts:
  Adafruit Feather M0 Basic Proto: At the Feather M0's heart is an ATSAMD21G18 ARM Cortex M0 processor, clocked at 48 MHz and at 3.3V logic, the same one used in the new Arduino Zero. This chip has a whopping 256K of FLASH (8x more than the Atmega328 or 32u4) and 32K of RAM (16x as much)! This chip comes with built in USB so it has USB-to-Serial program & debug capability built in with no need for an FTDI-like chip. To make it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
  Adafruit DS3231: The datasheet for the DS3231 explains that this part is an "Extremely Accurate I²C-Integrated RTC/TCXO/Crystal". And, hey, it does exactly what it says on the tin! This Real Time Clock (RTC) is the most precise you can get in a small, low power package. Most RTCs use an external 32kHz timing crystal that is used to keep time with low current draw. And that's all well and good, but those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
  I2C Non-Volatile FRAM 32KB: With our I2C FRAM breakout board you can add some FRAM storage to your next DIY project. FRAM allows for a lower power usage and a faster write performance. It's excellent for low-power or inconsistent-power datalogging or data buffering where you want to stream data fast while also keeping the data when there's no power. Unlike Flash or EEPROM there's no pages to worry about. Each byte can be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
